// Logisim project imm-gen.circ as structural Verilog: 1 circuit, main circuit imm_gen
module imm_gen (
  input  [31:0] Instruction,
  input  [2:0] ImmSel,
  output [31:0] Immediate
);

  wire [31:0] shifter_1_out;

  Shifter #(.shift("ar"), .width(32)) shifter_1 (.in(Instruction), .\dist (5'b10100), .out(shifter_1_out));
  Multiplexer #(.select(3), .width(32)) multiplexer_1 (
    .in0(shifter_1_out), .out(Immediate), .sel(ImmSel));  // open: in1, in2, in3, in4, in5, in6, in7

  // Notes on the sheet:
  //   INPUTS to your circuit
  //   DON'T CHANGE THE LOCATIONS OF THE INPUTS AND OUTPUTS!
  //   OUTPUT from your circuit
endmodule
